# Fritzing sketch Pro mini nrf24 lcd relais V1.11 straight (saved by Fritzing 0.9.2b)
circuit board: 6.41893cm x 4.12455cm

parts:
  LCD1 = LCD screen
  J2 = female pin header, 3 pins [form="♀ (female)"]
  R1 = Trimmer Potentiometer [maximum_resistance=10kΩ package=THT]
  J1 = male pin header, 2 pins [form="♂ (male)"]
  NRF24L01+ = double row female pin header, 8 pins [form="♀ (female)"]
  Pro_mini = Arduino Pro Mini v13
  J4 = female pin header, 5 pins [form="♀ (female)"]
  D1 = Rectifier Diode [part_number="zener 5.1V" package="300 mil [THT]"]
  R2 = Resistor [tolerance=±5% resistance=4.7k package=THT]  # not connected
  J5 = Generic male header - 3 pins [form="♂ (male)" package=THT]
  C1 = Film Capacitor MKT Box Type

nets:
  VSS: LCD1.VSS, LCD1.R/W, J2.pin1, R1.leg2, J1.pin1, NRF24L01+.pin1, Pro_mini.GND, J4.pin2, D1.anode, J5.pin1, J5.pin2, C1.2
  VDD: LCD1.VDD, J2.pin2, Pro_mini.VCC
  N1: LCD1.V0, R1.wiper
  N2: LCD1.RS, Pro_mini.D2
  N3: LCD1.E, Pro_mini.D3_PWM
  N4: LCD1.DB4, Pro_mini.D4
  N5: LCD1.DB5, Pro_mini.D5_PWM
  N6: LCD1.DB6, Pro_mini.D7
  N7: LCD1.DB7, Pro_mini.D8
  N8: LCD1.LED-, J1.pin2
  N9: R1.leg1, J4.pin1
  N10: NRF24L01+.pin2, Pro_mini.D9_PWM
  N11: NRF24L01+.pin3, Pro_mini.D13/SCK
  N12: NRF24L01+.pin4, Pro_mini.D12/MISO
  N13: NRF24L01+.pin6, Pro_mini.D11_PWM/MOSI
  N14: NRF24L01+.pin7, Pro_mini.D10_PWM/SS
  N15: Pro_mini.RAW, J5.pin3
  N16: Pro_mini.A3, J4.pin5
  N17: Pro_mini.A2, J4.pin4
  N18: Pro_mini.A1, J4.pin3
  N19: Pro_mini.A0, D1.cathode, C1.1

notes:
  - + in
  Relay
  jmp
  A  B  C  D  E  F  G  H  I  J  K  L  M  N  O  P  Q  R  S  T  U  V  W  X
  + - 1 2 3
  01 02 03 04 05 06 07 08 09 10 11 12 13 14 15 16 17 18
  5V 3V - 5V
  - - 5V
  C-
  C+
  R- R+
  R
  - - - -
  Rl
  led
  -
  +
  - - -
  J6
  jmp1b
  jmp2
  hfmv
  V 1.11
  nRF24L01+/pro mini/lcd/relay str
  jmp4b

custom parts:
  Arduino Pro Mini v13: It's blue! It's thin! It's the Arduino Pro Mini! SparkFun's minimal design approach to Arduino. This is a 5V Arduino running the 16MHz bootloader. Arduino Pro Mini does not come with connectors populated so that you can solder in any connector or wire with any orientation you need. We recommend first time Arduino users start with the Uno R3. It's a great board that will get you up and running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
  Generic male header - 3 pins: Generic male header
  Film Capacitor MKT Box Type: Film Metalized Capacitor MKT Box Type. Large
