# Fritzing sketch Simple Thermostat principle schem (saved by Fritzing 0.9.2b)

parts:
  Part1 = Arduino Pro Mini v13
  LCD1 = LCD screen
  U1 = mystery part, 3 pins [chip_label="5 to 3.3V"]
  ANT1 = Antenna  # not connected
  U3 = mystery part, 8 pins [chip_label=NRF24L01]
  J2 = female pin header, 3 pins [form="♀ (female)"]  # not connected
  J1 = male pin header, 2 pins [form="♂ (male)"]
  R1 = Trimmer Potentiometer [maximum_resistance=10kΩ package=THT]
  led = LED - 5mm [color="Red (633nm)" package="5 mm [THT]"]
  K1 = Relay [part_number=FRS1B-S package=THT]
  jmp2 = male pin header, 2 pins [form="♂ (male)"]
  S1 = Pushbutton [package=THT]
  J6 = female pin header, 2 pins [form="♀ (female)"]
  U6 = mystery part, 2 pins [chip_label=?]
  J15 = male pin header, 3 pins [form="♂ (male)"]
  Rl = Resistor [tolerance=±5% resistance=220 package=THT]
  J4 = female pin header, 5 pins [form="♀ (female)"]
  J5 = male pin header, 5 pins [form="♂ (male)"]
  J17 = female pin header, 4 pins [form="♀ (female)"]
  J18 = male pin header, 4 pins [form="♂ (male)"]
  S2 = Toggle Switch [package=THT]
  U7 = mystery part, 6 pins [chip_label=?]
  J23 = screw terminal, 4 pins
  J22 = screw terminal, 4 pins
  U8 = mystery part, 2 pins [chip_label=?]
  R = Resistor [tolerance=±5% resistance=10k package=THT]
  NTC = Resistor [tolerance=±5% resistance=10k package=THT]
  C = Tantalum Capacitor [capacitance=47µF package="100 mil [THT, tantalum]"]  # not connected
  jmp3 = male pin header, 2 pins [form="♂ (male)"]
  J19 = screw terminal, 3 pins
  J16 = screw terminal, 3 pins

nets:
  N1: Part1.RAW, U1.pin1, J4.pin1
  N2: Part1.GND, J1.pin1
  N3: Part1.RESET, jmp2.pin1
  N4: Part1.A3, jmp2.pin2, J4.pin5, jmp3.pin2
  N5: Part1.A2, J4.pin4
  N6: Part1.A1, J4.pin3
  N7: Part1.A0, R.Pin_1
  N8: Part1.D13/SCK, Part1.D9_PWM, U3.pin3, U3.pin7
  N9: Part1.D8, Part1.D7, LCD1.DB6, LCD1.DB7
  N10: Part1.D6_PWM, LCD1.LED+
  N11: Part1.D5_PWM, Part1.D4, LCD1.DB4, LCD1.DB5
  N12: Part1.D3_PWM, LCD1.E
  N13: Part1.D2, LCD1.RS
  N14: LCD1.V0, R1.wiper
  N15: LCD1.LED-, J1.pin2
  N16: U1.pin3, U3.pin2
  N17: led.cathode, jmp3.pin1
  N18: K1.A, J16.pin1
  N19: K1.COIL1, J5.pin3
  N20: K1.C1, K1.C2, J16.pin2
  N21: K1.B, J16.pin3
  N22: S1.leg0, J6.pin2
  N23: S1.leg1, J6.pin1
  N24: U6.pin1, J23.pin1
  N25: U6.pin2, J23.pin2
  N26: J15.pin2, NTC.Pin_0
  N27: J15.pin3, NTC.Pin_1
  N28: Rl.Pin_0, J18.pin2, R.Pin_0
  N29: J17.pin1, J22.pin4
  N30: J17.pin2, J22.pin3
  N31: J17.pin3, J22.pin2, U8.pin1
  N32: J17.pin4, J22.pin1, U8.pin2
  N33: J18.pin1, S2.L1
  N34: J18.pin3, J19.pin2
  N35: J18.pin4, J19.pin1
  N36: U7.pin1, J23.pin4
  N37: U7.pin6, J23.pin3

notes:
  5 to 3.3V
  NRF24L01+
  to RAW or VCC,
  See only Schematic overview, PCB in separate file
  PCB in separate Fritzing file
  Most connections to GND and +5V are not shown
  valve
  pump motor
  230 V
  Honeywell
  optional
  230V to 5V USB
  Heater
  thermostat
  NO
  COM
  Optional/Unused
  Simple Thermostat
  Principle schem
  jmp1a or jmp1b=
  jmp1a used
  NC
  20-12-2015 hfmv V1.0

custom parts:
  Arduino Pro Mini v13: It's blue! It's thin! It's the Arduino Pro Mini! SparkFun's minimal design approach to Arduino. This is a 5V Arduino running the 16MHz bootloader. Arduino Pro Mini does not come with connectors populated so that you can solder in any connector or wire with any orientation you need. We recommend first time Arduino users start with the Uno R3. It's a great board that will get you up and running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
